# Fritzing sketch M1_cardio_v2 (saved by Fritzing 0.9.3b)
breadboards: 2

parts:
  U1 = LM124-324 Quad Opamp [package="DIP (Dual Inline)"]
  LED1 = LED - 5mm [color="Red (633nm)" package="5 mm [THT]"]
  C1 = Tantalum Capacitor [capacitance="1 μF" package="B 3528 [SMD, tantalum]"]
  C2 = Tantalum Capacitor [capacitance="1 μF" package="B 3528 [SMD, tantalum]"]
  R1 = Resistor [tolerance=±5% resistance=2.2k package="0603 [SMD]"]
  R2 = Resistor [tolerance=±5% resistance=1k package="0603 [SMD]"]
  R3 = Resistor [tolerance=±5% resistance=68k package="0603 [SMD]"]
  R5 = Resistor [tolerance=±5% resistance=100 package="0603 [SMD]"]
  R6 = Resistor [tolerance=±5% resistance=470k package="0603 [SMD]"]
  Composant2 = Arduino Micro (Rev3)
  LED2 = LED - 5mm [color="Infrared (940nm)" package="5 mm [THT]"]
  Q1 = LTR-301 [package=ltr-301]
  R4 = Resistor [tolerance=±5% resistance=22k package="0603 [SMD]"]

nets:
  N1: U1.VCC+, R1.Pin_1, Composant2.5V, R4.Pin_0
  N2: U1.2IN+, C1.-, R3.Pin_0
  N3: U1.2IN-, C2.+, R2.Pin_0, R6.Pin_1
  N4: U1.2OUT, C2.-, R5.Pin_1, R6.Pin_0
  N5: U1.VCC-, LED1.cathode, R2.Pin_1, R3.Pin_1, Composant2.GND, LED2.cathode, Q1.C
  N6: LED1.anode, R5.Pin_0, Composant2.A0
  N7: R1.Pin_0, LED2.anode
  N8: Q1.E, R4.Pin_1
